# Fritzing sketch Untitled Sketch (saved by Fritzing 0.9.1b)
breadboards: 1

parts:
  Part1 = Arduino Mega 2560 (Rev3)
  LCD1 = LCD screen
  R1 = Trimmer Potentiometer [maximum_resistance=10kΩ package=THT]
  RE1 = Rotary Encoder [package=THT]
  LED1 = RGB LED (com. cathode, rgb) [package="5 mm [THT]"]
  R2 = Resistor [tolerance=±5% resistance=220 package=THT]
  S1 = Pushbutton [package="[THT]"]
  R3 = Resistor [tolerance=±5% resistance=220 package=THT]

nets:
  N1: Part1.D10_PWM, LED1.blue_anode
  N2: Part1.D9_PWM, LED1.green_anode
  N3: Part1.D8_PWM, LED1.red_anode
  5V: Part1.5V, LCD1.VDD, LCD1.LED+, R1.leg1, R3.Pin_1
  GND: Part1.GND, LCD1.VSS, LCD1.R/W, LCD1.LED-, R1.leg2, R2.Pin_1, S1.Pin_3, S1.Pin_4
  N4: Part1.D5_PWM, RE1.EncoderPinA, S1.Pin_1, S1.Pin_2, R3.Pin_0
  N5: Part1.D6_PWM, RE1.EncoderPinC
  N6: Part1.D7_PWM, RE1.EncoderPinB
  N7: Part1.D38, LCD1.RS
  N8: Part1.D41, LCD1.E
  N9: Part1.D44, LCD1.DB4
  N10: Part1.D47, LCD1.DB5
  N11: Part1.D48, LCD1.DB6
  N12: Part1.D50, LCD1.DB7
  N13: LCD1.V0, R1.wiper
  N14: LED1.common_cathode, R2.Pin_0
